# Fritzing sketch circuit (saved by Fritzing 0.9.1b)
breadboards: 1

parts:
  Raspberry_Pi = Raspberry Pi B+
  1000µF_capacitor = Capacitor Polarized [package=cpol-radial-10uf-25v]
  3V/5V_Level_Shifter = OP482 - Low Power, High Speed JFET Quad Operational Amplifier [part_number=OP482]
  5V_DC_power = 2.1mm Barrel Jack with Terminal Block
  Neopixel_strip = Neopixel Strip -- Black (30/m)

nets:
  GND: Raspberry_Pi.GND, 1000µF_capacitor.-, 3V/5V_Level_Shifter.OUTA, 3V/5V_Level_Shifter.OUTB, 5V_DC_power.NEG, Neopixel_strip.GND
  N1: Raspberry_Pi.GPIO18, 3V/5V_Level_Shifter.+INA
  5V: Raspberry_Pi.5V, 1000µF_capacitor.+, 3V/5V_Level_Shifter.OUTD, 5V_DC_power.POS, Neopixel_strip.+5V
  N2: 3V/5V_Level_Shifter.-INA, Neopixel_strip.Din

notes:
  +5V, ground DC distributed along row 5

custom parts:
  Neopixel Strip -- Black (30/m): These NeoPixel strips have 30 digitally-addressable pixel LEDs per meter and are very affordable and are only 12.5 mm wide, 10 mm if you remove the strip from the casing.
